# Fritzing sketch 7805+Zener (saved by Fritzing 0.9.0b)
breadboards: 1

parts:
  U1 = Voltage Regulator - 5V [package="TO220 [THT]"]
  VCC1 = Battery block 9V
  VCC2 = Battery block 9V
  U2 = mystery part, 3 pins [chip_label=TL431]
  C1 = Electrolytic Capacitor [capacitance=10µF package="100 mil [THT, electrolytic]"]
  C2 = Ceramic Capacitor [capacitance=100nF package="100 mil [THT, multilayer]"]
  C3 = Electrolytic Capacitor [capacitance=1µF package="100 mil [THT, electrolytic]"]
  R2 = Resistor [tolerance=±5% resistance=100 package=THT]
  R4 = Resistor [tolerance=±5% resistance=220 package=THT]
  D1 = Zener Diode [part_number=1N4732A breakdown_voltage=3.6V package="300 mil [THT]"]
  C4 = Ceramic Capacitor [capacitance=100nF package="100 mil [THT, multilayer]"]
  D2 = Schottky Diode [part_number=1N5817 package="Melf DO-213 AB [SMD]"]
  R5 = Resistor [tolerance=±5% resistance=330 package=THT]
  R6 = Resistor [tolerance=±5% resistance=220 package=THT]

nets:
  N1: U1.input_voltage, VCC1.+, C1.+, C2.1, D2.cathode
  N2: U1.GND, U2.pin2, R2.Pin_1, R6.Pin_1
  N3: U1.output_voltage, C3.+, R4.Pin_0, C4.0, D2.anode, R6.Pin_0
  N4: VCC1.-, VCC2.+, U2.pin1, U2.pin3
  N5: VCC2.-, R2.Pin_0
  N6: C1.-, C2.0
  N7: C3.-, D1.anode, C4.1, R5.Pin_0
  N8: R4.Pin_1, D1.cathode, R5.Pin_1

notes:
  10.5V
  負電源
  GND
  GND
  正電源
