# Fritzing sketch Connection-Test (saved by Fritzing 0.9.0b)
perfboards: 4

parts:
  J1 = female pin header, 1 pin [form="♀ (female)"]
  J2 = female pin header, 1 pin [form="♀ (female)"]
  J3 = female pin header, 1 pin [form="♀ (female)"]
  J4 = female pin header, 1 pin [form="♀ (female)"]
  J5 = female pin header, 1 pin [form="♀ (female)"]
  J6 = female pin header, 1 pin [form="♀ (female)"]
  J7 = female pin header, 1 pin [form="♀ (female)"]  # not connected
  J8 = female pin header, 1 pin [form="♀ (female)"]
  J10 = female pin header, 3 pins [form="♀ (female)"]
  J11 = female pin header, 3 pins [form="♀ (female)"]
  J12 = female pin header, 3 pins [form="♀ (female)"]
  J13 = female pin header, 4 pins [form="♀ (female)"]
  J14 = Power Jack [package=power_jack_pth_lock]
  J15 = Power Jack [package=power_jack_pth_lock]
  J16 = female pin header, 3 pins [form="♀ (female)"]
  J17 = female pin header, 4 pins [form="♀ (female)"]
  J18 = screw terminal, 3 pins
  J19 = female pin header, 2 pins [form="♀ (female)"]
  J20 = screw terminal, 3 pins
  J21 = female pin header, 7 pins [form="♀ (female)"]
  J22 = BANANA_CONN [package=banana_conn]
  J24 = BANANA_CONN [package=banana_conn]
  J25 = BANANA_CONN [package=banana_conn]
  U1 = LCD-16X2 [package=lcd-8x2]  # not connected
  J26 = female pin header, 7 pins [form="♀ (female)"]
  U2 = POT [package=pot_alpha_rv16af-20]
  U3 = POT [package=pot_alpha_rv16af-20]
  J27 = female pin header, 3 pins [form="♀ (female)"]
  J28 = female pin header, 3 pins [form="♀ (female)"]
  U4 = SWITCH_SPDT [package=kps-1290]
  J29 = BANANA_CONN [package=banana_conn]  # not connected

nets:
  N1: J1.pin1, J14.GND, J18.pin3
  N2: J2.pin1, J14.GNDBREAK
  N3: J3.pin1, J15.GND, J18.pin2
  N4: J4.pin1, J15.GNDBREAK, J18.pin1
  N5: J5.pin1, J19.pin1, J22.1
  N6: J6.pin1, J20.pin1, U4.S
  N7: J8.pin1, J19.pin2, J25.1
  N8: J10.pin1, J12.pin1
  N9: J10.pin2, J12.pin2
  N10: J10.pin3, J12.pin3
  N11: J11.pin1, J16.pin3
  N12: J11.pin3, J16.pin1
  N13: J13.pin1, J17.pin4
  N14: J13.pin2, J17.pin3
  N15: J13.pin3, J17.pin2
  N16: J13.pin4, J17.pin1
  N17: J20.pin2, U4.O
  N18: J21.pin1, J26.pin1
  N19: J21.pin2, J26.pin2
  N20: J21.pin3, J26.pin3
  N21: J21.pin4, J26.pin4
  N22: J21.pin5, J26.pin5
  N23: J21.pin6, J26.pin6
  N24: J21.pin7, J26.pin7
  N25: J24.1, U4.P
  N26: U2.A, U2.S, J28.pin2
  N27: U2.E, J28.pin3
  N28: U3.A, U3.S, J27.pin2
  N29: U3.E, J27.pin3

notes:
  Dual Power Supply
  Meas Power Supply
  Digital Part
  Analog Part
